// Digital circuit ALU.dig as structural Verilog
module ALU (
  input  [3:0] in_1,
  input  [7:0] in_2,
  input  [7:0] in_3
);

  wire and_1_out, and_2_out, not_1_out, opcodes_1_dif, opcodes_1_out_0;
  wire [0:0] opcodes_1_out_1;
  wire [3:0] mut_plicador_1_p_3, mut_plicador_1_p_4;
  wire [7:0] or_1_out, undriven, undriven_2;

  opcodes opcodes_1 (.E(in_1), .Out_1(opcodes_1_out_1[0]), .Out_0(opcodes_1_out_0), .Dif(opcodes_1_dif));
  and and_1 (and_1_out, opcodes_1_out_0, not_1_out);
  not not_1 (not_1_out, opcodes_1_dif);
  and and_2 (and_2_out, opcodes_1_dif, opcodes_1_out_0);
  LED led_1 (.in(opcodes_1_out_1[0]));
  LED led_2 (.in(and_1_out));
  LED led_3 (.in(and_2_out));
  // And and_3 has open pins: In_1=or_1_out, In_2={{7{1'b0}}, opcodes_1_out_1[0]}, out=open
  assign or_1_out = in_2 | in_3;  // Or or_1, 8 bits wide
  mut_plicador mut_plicador_1 (
    .B(undriven_2), .A(undriven), .P_0(mut_plicador_1_p_3[0]), .P_1(mut_plicador_1_p_3[1]),
    .P_2(mut_plicador_1_p_3[2]), .P_3(mut_plicador_1_p_3[3]), .P_4(mut_plicador_1_p_4[0]),
    .P_5(mut_plicador_1_p_4[1]), .P_6(mut_plicador_1_p_4[2]), .P_7(mut_plicador_1_p_4[3]));  // open: P_8, P_9, P_10, P_11, P_12, P_13, P_14, P_15
  Samador8bits samador8bits_1 (.C_0(mut_plicador_1_p_3), .C_1(mut_plicador_1_p_4));  // open: E_0, E_1
  // subtrator8bit subtrator8bit_1: pin names not known; wires that end beside it: mut_plicador_1_p_3, mut_plicador_1_p_4
  Seven_Seg_Hex seven_seg_hex_1 (.d(mut_plicador_1_p_3), .dp(1'b0));
  Seven_Seg_Hex seven_seg_hex_2 (.d(mut_plicador_1_p_4), .dp(1'b0));
endmodule
